// Logisim project LAB 10 ES 1 contatore.circ as structural Verilog: 3 circuits, main circuit add mod 8
module add_mod_8 (
  input  [2:0] Q,
  output [2:0] Q_prime
);

  wire and_1_out;

  not not_1 (Q_prime[0], Q[0]);
  xor xor_1 (Q_prime[1], Q[0], Q[1]);
  and and_1 (and_1_out, Q[0], Q[1]);
  xor xor_2 (Q_prime[2], and_1_out, Q[2]);
endmodule

module display (
  input  [3:0] in_1
);

  Hex_Digit_Display hex_digit_display_1 (.value(in_1));  // open: dp
endmodule

module contatore (
  input  clk
);

  wire [2:0] add_mod_8_1_q_prime, d_ff_1_q;

  add_mod_8 add_mod_8_1 (.Q(d_ff_1_q), .Q_prime(add_mod_8_1_q_prime));
  D_Flip_Flop d_ff_1 (.clk(clk), .D(add_mod_8_1_q_prime[0]), .Q(d_ff_1_q[0]));  // open: Qn, preset, en, reset
  D_Flip_Flop d_ff_2 (.clk(clk), .D(add_mod_8_1_q_prime[1]), .Q(d_ff_1_q[1]));  // open: Qn, preset, en, reset
  D_Flip_Flop d_ff_3 (.clk(clk), .D(add_mod_8_1_q_prime[2]), .Q(d_ff_1_q[2]));  // open: Qn, preset, en, reset
  Hex_Digit_Display hex_digit_display_1 (.value({1'b0, d_ff_1_q}));  // open: dp
endmodule
