// Logisim project LAB 10 ES 2 OROLOGIO.circ as structural Verilog: 5 circuits, main circuit adder mod 16
module adder_mod_16 (
  input  [3:0] Q,
  output [3:0] Q_prime
);

  wire and_1_out, and_2_out;

  not not_1 (Q_prime[0], Q[0]);
  xor xor_1 (Q_prime[1], Q[0], Q[1]);
  and and_1 (and_1_out, Q[0], Q[1]);
  and and_2 (and_2_out, Q[0], Q[1], Q[2]);
  xor xor_2 (Q_prime[2], and_1_out, Q[2]);
  xor xor_3 (Q_prime[3], and_2_out, Q[3]);
endmodule

module contatore (
  input  clk,
  input  reset,
  output [3:0] count
);

  wire [3:0] adder_mod_16_1_q_prime;

  adder_mod_16 adder_mod_16_1 (.Q(count), .Q_prime(adder_mod_16_1_q_prime));
  D_Flip_Flop d_ff_1 (.clk(clk), .D(adder_mod_16_1_q_prime[0]), .Q(count[0]), .reset(reset));  // open: Qn, preset, en
  D_Flip_Flop d_ff_2 (.clk(clk), .D(adder_mod_16_1_q_prime[1]), .Q(count[1]), .reset(reset));  // open: Qn, preset, en
  D_Flip_Flop d_ff_3 (.clk(clk), .D(adder_mod_16_1_q_prime[2]), .Q(count[2]), .reset(reset));  // open: Qn, preset, en
  D_Flip_Flop d_ff_4 (.clk(clk), .D(adder_mod_16_1_q_prime[3]), .Q(count[3]), .reset(reset));  // open: Qn, preset, en
  Hex_Digit_Display hex_digit_display_1 (.value(count));  // open: dp
endmodule

module stop_9 (
  input  [3:0] count,
  output reset
);

  and and_1 (reset, ~count[0], count[1], ~count[2], count[3]);  // AND_Gate
endmodule

module stop_5 (
  input  [3:0] count,
  output reset
);

  and and_1 (reset, ~count[0], count[1], count[2], ~count[3]);  // AND_Gate
endmodule

module orologio (
);

  wire clock_1_out, stop_5_1_reset, stop_5_2_reset, stop_9_1_reset, stop_9_2_reset;
  wire [3:0] contatore_1_count, contatore_2_count, contatore_3_count, contatore_4_count;

  Clock clock_1 (.out(clock_1_out));
  stop_5 stop_5_1 (.count(contatore_1_count), .reset(stop_5_1_reset));
  Hex_Digit_Display hex_digit_display_1 (.value(contatore_1_count));  // open: dp
  contatore contatore_1 (.clk(stop_9_1_reset), .reset(stop_5_1_reset), .count(contatore_1_count));
  stop_9 stop_9_1 (.count(contatore_3_count), .reset(stop_9_1_reset));
  Hex_Digit_Display hex_digit_display_2 (.value(contatore_3_count));  // open: dp
  contatore contatore_2 (.clk(stop_9_2_reset), .reset(stop_5_2_reset), .count(contatore_2_count));
  contatore contatore_3 (.clk(stop_5_2_reset), .reset(stop_9_1_reset), .count(contatore_3_count));
  stop_5 stop_5_2 (.count(contatore_2_count), .reset(stop_5_2_reset));
  Hex_Digit_Display hex_digit_display_3 (.value(contatore_4_count));  // open: dp
  Hex_Digit_Display hex_digit_display_4 (.value(contatore_2_count));  // open: dp
  contatore contatore_4 (.clk(clock_1_out), .reset(stop_9_2_reset), .count(contatore_4_count));
  stop_9 stop_9_2 (.count(contatore_4_count), .reset(stop_9_2_reset));
endmodule
