// Logisim project LAB 10 ES 3 - RANDOM.circ as structural Verilog: 1 circuit, main circuit main
module main (
  input  [3:0] seed,
  input  write
);

  wire clock_1_out, multiplexer_1_out, multiplexer_2_out, multiplexer_3_out, multiplexer_4_out, xor_1_out;
  wire [3:0] d_ff_1_q;

  Clock clock_1 (.out(clock_1_out));
  xor xor_1 (xor_1_out, d_ff_1_q[2], d_ff_1_q[3]);
  Multiplexer #(.enable("false")) multiplexer_1 (.in0(xor_1_out), .in1(seed[0]), .out(multiplexer_1_out), .sel(write));
  D_Flip_Flop d_ff_1 (.clk(clock_1_out), .D(multiplexer_1_out), .Q(d_ff_1_q[0]));  // open: Qn, preset, en, reset
  D_Flip_Flop d_ff_2 (.clk(clock_1_out), .D(multiplexer_2_out), .Q(d_ff_1_q[1]));  // open: Qn, preset, en, reset
  Multiplexer #(.enable("false")) multiplexer_2 (
    .in0(d_ff_1_q[0]), .in1(seed[1]), .out(multiplexer_2_out), .sel(write));
  Multiplexer #(.enable("false")) multiplexer_3 (
    .in0(d_ff_1_q[1]), .in1(seed[2]), .out(multiplexer_3_out), .sel(write));
  D_Flip_Flop d_ff_3 (.clk(clock_1_out), .D(multiplexer_3_out), .Q(d_ff_1_q[2]));  // open: Qn, preset, en, reset
  D_Flip_Flop d_ff_4 (.clk(clock_1_out), .D(multiplexer_4_out), .Q(d_ff_1_q[3]));  // open: Qn, preset, en, reset
  Multiplexer #(.enable("false")) multiplexer_4 (
    .in0(d_ff_1_q[2]), .in1(seed[3]), .out(multiplexer_4_out), .sel(write));
  Hex_Digit_Display hex_digit_display_1 (.value(d_ff_1_q));  // open: dp
endmodule
