// Logisim project LAB 4 ES 1 POS.circ as structural Verilog: 1 circuit, main circuit main
module main (
  input  A,
  input  B,
  output A_XNOR_B
);

  wire or_1_out, or_2_out;

  or or_1 (or_1_out, A, ~B);  // OR_Gate
  or or_2 (or_2_out, ~A, B);  // OR_Gate
  and and_1 (A_XNOR_B, or_1_out, or_2_out);
endmodule
