// Logisim project LAB 4 ES 1 SOP.circ as structural Verilog: 1 circuit, main circuit main
module main (
  input  A,
  input  B,
  output A_XNOR_B,
  output out_4,
  output out_5
);

  wire and_1_out, and_2_out, and_3_out, nor_1_out;

  and and_1 (and_1_out, ~A, ~B);  // AND_Gate
  and and_2 (and_2_out, A, B);
  nor nor_1 (nor_1_out, A, B);
  and and_3 (and_3_out, A, B);
  or or_1 (A_XNOR_B, and_1_out, and_2_out);
  or or_2 (out_5, nor_1_out, and_3_out);
  xnor xnor_1 (out_4, A_XNOR_B, out_5);
endmodule
