// Logisim project LAB 4 ES 2.circ as structural Verilog: 1 circuit, main circuit main
module main (
  input  A,
  input  B,
  input  C,
  input  D,
  output z3,
  output X,
  output z4,
  output EQ
);

  wire and_2_out, and_3_out, and_4_out, and_5_out, and_6_out, and_7_out, and_8_out, and_9_out, and_10_out,
       and_11_out, and_12_out, or_1_out, or_2_out, or_3_out, or_4_out, or_6_out, or_7_out;

  or or_1 (or_1_out, A, ~B);  // OR_Gate
  or or_2 (or_2_out, B, C);
  and and_1 (z4, ~B, D);  // AND_Gate
  and and_2 (and_2_out, ~A, ~B, ~C, D);  // AND_Gate
  and and_3 (and_3_out, ~A, ~B, C, D);  // AND_Gate
  and and_4 (and_4_out, A, ~B, ~C, D);  // AND_Gate
  and and_5 (and_5_out, A, ~B, C, ~D);  // AND_Gate
  and and_6 (and_6_out, A, ~B, C, D);  // AND_Gate
  and and_7 (and_7_out, A, B, ~C, ~D);  // AND_Gate
  and and_8 (and_8_out, A, B, ~C, D);  // AND_Gate
  and and_9 (and_9_out, A, B, C, ~D);  // AND_Gate
  and and_10 (and_10_out, A, B, C, D);
  or or_3 (or_3_out, B, C);
  or or_4 (or_4_out, A, ~B);  // OR_Gate
  and and_11 (and_11_out, A, or_3_out);
  and and_12 (and_12_out, or_4_out, D);
  and and_13 (z3, A, or_1_out, or_2_out);
  or or_5 (X, z3, z4);
  or or_6 (or_6_out, and_11_out, and_12_out);
  or or_7 (or_7_out, and_2_out, and_3_out, and_4_out, and_5_out, and_6_out, and_7_out, and_8_out, and_9_out, and_10_out);
  NotExactlyOne xnor_1 (.out(EQ), .in0(X), .in1(or_7_out), .in2(or_6_out));
endmodule
