// Logisim project LAB 5 ES 1 MUX.circ as structural Verilog: 2 circuits, main circuit Decodificatore a 2 bit
module Decodificatore_a_2_bit (
  input  b1,
  input  b2,
  output y1,
  output y2,
  output y3,
  output y4
);

  and and_1 (y1, ~b1, ~b2);  // AND_Gate
  and and_2 (y2, ~b1, b2);  // AND_Gate
  and and_3 (y3, b1, ~b2);  // AND_Gate
  and and_4 (y4, b1, b2);
endmodule

module Mux_4_vie (
  input  [3:0] in_1,
  input  a,
  input  b,
  output out_4
);

  wire and_1_out, and_2_out, and_3_out, and_4_out, decodificatore_a_2_bit_1_y1, decodificatore_a_2_bit_1_y2,
       decodificatore_a_2_bit_1_y3, decodificatore_a_2_bit_1_y4;

  Decodificatore_a_2_bit decodificatore_a_2_bit_1 (
    .b1(a), .b2(b), .y1(decodificatore_a_2_bit_1_y1), .y2(decodificatore_a_2_bit_1_y2),
    .y3(decodificatore_a_2_bit_1_y3), .y4(decodificatore_a_2_bit_1_y4));
  and and_1 (and_1_out, in_1[0], decodificatore_a_2_bit_1_y1);
  and and_2 (and_2_out, in_1[1], decodificatore_a_2_bit_1_y2);
  and and_3 (and_3_out, in_1[2], decodificatore_a_2_bit_1_y3);
  and and_4 (and_4_out, in_1[3], decodificatore_a_2_bit_1_y4);
  or or_1 (out_4, and_1_out, and_2_out, and_3_out, and_4_out);
endmodule
