// Logisim project LAB 5 ES 3 FULL ADDER.circ as structural Verilog: 1 circuit, main circuit Full Adder
module Full_Adder (
  input  R_in,
  input  A,
  input  B,
  output S,
  output R_out
);

  wire and_1_out, and_2_out, and_3_out, and_4_out, and_5_out, and_6_out, and_7_out;

  and and_1 (and_1_out, ~R_in, ~A, B);  // AND_Gate
  and and_2 (and_2_out, ~R_in, A, ~B);  // AND_Gate
  and and_3 (and_3_out, R_in, ~A, ~B);  // AND_Gate
  and and_4 (and_4_out, R_in, A, B);
  and and_5 (and_5_out, ~R_in, A, B);  // AND_Gate
  and and_6 (and_6_out, R_in, ~A, B);  // AND_Gate
  and and_7 (and_7_out, R_in, A, ~B);  // AND_Gate
  or or_1 (S, and_1_out, and_2_out, and_3_out, and_4_out);
  or or_2 (R_out, and_5_out, and_6_out, and_7_out, and_4_out);
endmodule
