// Logisim project LAB 6 ES 4 ADDIZIONATORE 4 BIT.circ as structural Verilog: 1 circuit, main circuit Addizionatore a 4 bit
module Addizionatore_a_4_bit (
  input  [3:0] A,
  input  [3:0] B,
  output [4:0] A_B
);

  wire adder_1_cout, adder_2_cout, half_adder_1_r;

  Half_Adder half_adder_1 (.A(A[0]), .B(B[0]), .S(A_B[0]), .R(half_adder_1_r));
  Adder #(.width(1)) adder_1 (.a(A[1]), .b(B[1]), .out(A_B[1]), .cin(half_adder_1_r), .cout(adder_1_cout));
  Adder #(.width(1)) adder_2 (.a(A[2]), .b(B[2]), .out(A_B[2]), .cin(adder_1_cout), .cout(adder_2_cout));
  Adder #(.width(1)) adder_3 (.a(A[3]), .b(B[3]), .out(A_B[3]), .cin(adder_2_cout), .cout(A_B[4]));
endmodule
