// Logisim project LAB 6 ES 7 overflow.circ as structural Verilog: 1 circuit, main circuit main
module main (
  input  [3:0] B,
  input  [3:0] A,
  input  S,
  output [3:0] OUT,
  output out_5,
  output overflow
);

  wire xor_5_out, xor_6_out;
  wire [3:0] xor_4_out;

  xor xor_1 (xor_4_out[3], S, B[3]);
  Adder #(.width(4)) adder_1 (.a(xor_4_out), .b(A), .out(OUT), .cin(S), .cout(out_5));
  xor xor_2 (xor_4_out[1], S, B[1]);
  xor xor_3 (xor_4_out[2], S, B[2]);
  xor xor_4 (xor_4_out[0], S, B[0]);
  xor xor_5 (xor_5_out, xor_4_out[3], OUT[3]);
  xor xor_6 (xor_6_out, OUT[3], A[3]);
  and and_1 (overflow, xor_5_out, xor_6_out);
endmodule
