// Logisim project LAB 7 ES 2 - ALU.circ as structural Verilog: 3 circuits, main circuit MULT 4 BIT
module MULT_4_BIT (
  input  [3:0] a,
  input  [3:0] b,
  output [7:0] out_3,
  output overflow
);

  wire adder_1_cout, adder_2_cout, adder_2_out, adder_3_cout, adder_4_cout, adder_4_out, adder_5_cout,
       adder_5_out, adder_6_cout, adder_6_out, adder_7_cout, adder_8_cout, adder_8_out, adder_9_cout,
       adder_9_out, adder_10_cout, adder_10_out, adder_11_cout, adder_11_out, adder_12_cout, adder_13_cout,
       adder_13_out, adder_14_cout, adder_14_out, adder_15_cout, adder_15_out, adder_16_cout, adder_16_out,
       adder_17_cout, adder_18_cout, adder_18_out, adder_19_cout, adder_19_out, adder_20_cout, adder_20_out,
       adder_21_cout, adder_22_out, b0a1_out, b0a2_out, b0a3_out, b1a0_out, b1a1_out, b1a2_out, b1a3_out,
       b2a0_out, b2a1_out, b2a2_out, b2a3_out, b3a0_out, b3a1_out, b3a2_out, b3a3_out;

  and b3a2 (b3a2_out, a[2], b[3]);
  and b3a3 (b3a3_out, a[3], b[3]);
  and b3a1 (b3a1_out, a[1], b[3]);
  and b3a0 (b3a0_out, a[0], b[3]);
  and b2a2 (b2a2_out, a[2], b[2]);
  and b2a3 (b2a3_out, a[3], b[2]);
  and b2a1 (b2a1_out, a[1], b[2]);
  and b2a0 (b2a0_out, a[0], b[2]);
  and b1a3 (b1a3_out, a[3], b[1]);
  and b1a2 (b1a2_out, a[2], b[1]);
  and b1a1 (b1a1_out, a[1], b[1]);
  and b1a0 (b1a0_out, a[0], b[1]);
  and b0a3 (b0a3_out, a[3], b[0]);
  and b0a2 (b0a2_out, a[2], b[0]);
  and b0a0 (out_3[0], a[0], b[0]);
  and b0a1 (b0a1_out, a[1], b[0]);
  Adder #(.width(1)) adder_1 (.a(b0a1_out), .b(b1a0_out), .out(out_3[1]), .cout(adder_1_cout));  // open: cin
  Adder #(.width(1)) adder_2 (.a(b0a2_out), .b(b1a1_out), .out(adder_2_out), .cin(adder_1_cout), .cout(adder_2_cout));
  Adder #(.width(1)) adder_3 (.a(adder_2_out), .b(b2a0_out), .out(out_3[2]), .cout(adder_3_cout));  // open: cin
  Adder #(.width(1)) adder_4 (
    .a(adder_2_cout), .b(b0a3_out), .out(adder_4_out), .cin(adder_3_cout), .cout(adder_4_cout));
  Adder #(.width(1)) adder_5 (.a(adder_4_out), .b(b1a2_out), .out(adder_5_out), .cout(adder_5_cout));  // open: cin
  Adder #(.width(1)) adder_6 (.a(adder_5_out), .b(b2a1_out), .out(adder_6_out), .cout(adder_6_cout));  // open: cin
  Adder #(.width(1)) adder_7 (.a(adder_6_out), .b(b3a0_out), .out(out_3[3]), .cout(adder_7_cout));  // open: cin
  Adder #(.width(1)) adder_8 (
    .a(adder_6_cout), .b(adder_5_cout), .out(adder_8_out), .cin(adder_7_cout), .cout(adder_8_cout));
  Adder #(.width(1)) adder_9 (.a(adder_8_out), .b(adder_4_cout), .out(adder_9_out), .cout(adder_9_cout));  // open: cin
  Adder #(.width(1)) adder_10 (.a(adder_9_out), .b(b1a3_out), .out(adder_10_out), .cout(adder_10_cout));  // open: cin
  Adder #(.width(1)) adder_11 (.a(adder_10_out), .b(b2a2_out), .out(adder_11_out), .cout(adder_11_cout));  // open: cin
  Adder #(.width(1)) adder_12 (.a(adder_11_out), .b(b3a1_out), .out(out_3[4]), .cout(adder_12_cout));  // open: cin
  Adder #(.width(1)) adder_13 (
    .a(adder_11_cout), .b(adder_10_cout), .out(adder_13_out), .cin(adder_12_cout), .cout(adder_13_cout));
  Adder #(.width(1)) adder_14 (
    .a(adder_13_out), .b(adder_9_cout), .out(adder_14_out), .cout(adder_14_cout));  // open: cin
  Adder #(.width(1)) adder_15 (
    .a(adder_14_out), .b(adder_8_cout), .out(adder_15_out), .cout(adder_15_cout));  // open: cin
  Adder #(.width(1)) adder_16 (.a(adder_15_out), .b(b2a3_out), .out(adder_16_out), .cout(adder_16_cout));  // open: cin
  Adder #(.width(1)) adder_17 (.a(adder_16_out), .b(b3a2_out), .out(out_3[5]), .cout(adder_17_cout));  // open: cin
  Adder #(.width(1)) adder_18 (
    .a(adder_16_cout), .b(adder_15_cout), .out(adder_18_out), .cin(adder_17_cout), .cout(adder_18_cout));
  Adder #(.width(1)) adder_19 (
    .a(adder_18_out), .b(adder_14_cout), .out(adder_19_out), .cout(adder_19_cout));  // open: cin
  Adder #(.width(1)) adder_20 (
    .a(adder_19_out), .b(adder_13_cout), .out(adder_20_out), .cout(adder_20_cout));  // open: cin
  Adder #(.width(1)) adder_21 (.a(adder_20_out), .b(b3a3_out), .out(out_3[6]), .cout(adder_21_cout));  // open: cin
  Adder #(.width(1)) adder_22 (
    .a(adder_20_cout), .b(adder_19_cout), .out(adder_22_out), .cin(adder_21_cout));  // open: cout
  Adder #(.width(1)) adder_23 (.a(adder_22_out), .b(adder_18_cout), .out(out_3[7]), .cout(overflow));  // open: cin

  // Notes on the sheet:
  //   s1
  //   s2
  //   s2
  //   s3
  //   s3
  //   s3
  //   s3
  //   s4
  //   s4
  //   s4
  //   s4
  //   s4
  //   s5
  //   s5
  //   s5
  //   s5
  //   s5
  //   s6
  //   s6
  //   s6
  //   s6
  //   s7
  //   s7
endmodule

module ALU (
  input  x,
  input  in_2,
  input  [3:0] A,
  input  [3:0] B,
  output [3:0] output_low,
  output [3:0] output_high,
  output overflow
);

  wire main_1_overflow, mult_4_bit_1_overflow;
  wire [3:0] main_1_out;
  wire [7:0] mult_4_bit_1_out_3;

  LAB_6_ES_7_overflow_main main_1 (
    .B(B), .A(A), .S(in_2), .OUT(main_1_out), .overflow(main_1_overflow));  // open: out_5
  MULT_4_BIT mult_4_bit_1 (.a(A), .b(B), .out_3(mult_4_bit_1_out_3), .overflow(mult_4_bit_1_overflow));
  Multiplexer #(.width(4)) multiplexer_1 (
    .in0(main_1_out), .in1(mult_4_bit_1_out_3[3:0]), .out(output_low), .sel(x));  // open: en
  or or_1 (overflow, main_1_overflow, mult_4_bit_1_overflow);
  Multiplexer #(.width(4)) multiplexer_2 (
    .in0(4'b0000), .in1(mult_4_bit_1_out_3[7:4]), .out(output_high), .sel(x));  // open: en
endmodule

module main (
  input  x,
  input  in_2,
  input  [3:0] A,
  input  [3:0] B,
  output [3:0] high,
  output [3:0] low,
  output overflow
);

  ALU alu_1 (.x(x), .in_2(in_2), .A(A), .B(B), .output_low(low), .output_high(high), .overflow(overflow));
endmodule
