// Logisim project LAB 7 ES 2 ALU - PROF QUADRI.circ as structural Verilog: 2 circuits, main circuit ALU
module ALU (
  input  [3:0] A,
  input  [3:0] B,
  input  in_3,
  input  x,
  output [3:0] R_low,
  output [3:0] R_high,
  output Overflow
);

  wire main_1_p5, or_1_out;
  wire [3:0] main_1_p4, main_2_p3, main_2_p4;

  // add_sub_C2_main main_1: pin names not known; wires that end beside it: A, B, in_3, main_1_p4, main_1_p5
  // mult_4bit_main main_2: pin names not known; wires that end beside it: A, B, main_2_p3, main_2_p4
  or or_1 (or_1_out, main_2_p4[0], main_2_p4[1], main_2_p4[2], main_2_p4[3]);
  Multiplexer #(.width(4)) multiplexer_1 (.in0(main_1_p4), .in1(main_2_p3), .out(R_low), .sel(x));  // open: en
  Multiplexer #(.width(4)) multiplexer_2 (.in0(4'b0000), .in1(main_2_p4), .out(R_high), .sel(x));  // open: en
  or or_2 (Overflow, or_1_out, main_1_p5);
endmodule

module main (
  input  [3:0] A,
  input  [3:0] B,
  input  in_3,
  input  x,
  output [3:0] out_5,
  output [3:0] out_6,
  output out_7
);

  ALU alu_1 (.A(A), .B(B), .in_3(in_3), .x(x), .R_low(out_6), .R_high(out_5), .Overflow(out_7));
endmodule
