// Logisim project LAB 8 ES 1 BISTABILE.circ as structural Verilog: 4 circuits, main circuit bistabile set reset
module bistabile_set_reset (
  input  reset,
  input  set,
  output Q,
  output nQ
);

  nor nor_1 (Q, reset, nQ);
  nor nor_2 (nQ, Q, set);
endmodule

module sop_x_0 (
  input  c,
  input  s,
  input  in_3,
  output Q
);

  wire and_1_out, and_2_out, and_3_out, and_4_out;

  and and_1 (and_1_out, ~c, ~s);  // AND_Gate
  and and_2 (and_2_out, ~c, s);  // AND_Gate
  and and_3 (and_3_out, Q, and_1_out);
  and and_4 (and_4_out, and_2_out, in_3);
  or or_1 (Q, and_3_out, and_4_out);
endmodule

module sop_x01 (
  input  c,
  input  s,
  output Q
);

  wire and_1_out;

  and and_1 (and_1_out, Q, ~c);  // AND_Gate
  or or_1 (Q, and_1_out, s);
endmodule

module bistabile_bottoni_e_tunnel (
  output Q,
  output nQ
);

  wire C_out, S_out;

  Button C (.out(C_out));
  Button S (.out(S_out));
  or or_1 (Q, C_out, nQ);
  or or_2 (nQ, S_out, Q);
endmodule
