// Logisim project LAB 8 ES 2 BISTABILE CLOCK.circ as structural Verilog: 1 circuit, main circuit bistabile clock
module bistabile_clock (
  input  C,
  input  CLOCK,
  input  S,
  output Q,
  output nQ
);

  wire and_1_out, and_2_out;

  and and_1 (and_1_out, C, CLOCK);
  bistabile_set_reset bistabile_set_reset_1 (.reset(and_1_out), .set(and_2_out), .Q(Q), .nQ(nQ));
  and and_2 (and_2_out, CLOCK, S);
endmodule
