// Logisim project LAB 8 ES 3 LATCH D.circ as structural Verilog: 1 circuit, main circuit main
module main (
  input  D,
  input  Clock,
  output Q,
  output nQ
);

  wire not_1_out;

  not not_1 (not_1_out, D);
  bistabile_clock bistabile_clock_1 (.C(not_1_out), .CLOCK(Clock), .S(D), .Q(Q), .nQ(nQ));
endmodule
