// Logisim project LAB 8 ES 4 MEMORIZZAZIONE 4 BIT.circ as structural Verilog: 1 circuit, main circuit main
module main (
  input  [3:0] INPUT,
  input  CLK,
  input  WRITE,
  output [3:0] OUTPUT
);

  wire and_1_out;

  and and_1 (and_1_out, CLK, WRITE);
  LAB_8_ES_3_LATCH_D_main main_1 (.D(INPUT[0]), .Clock(and_1_out), .Q(OUTPUT[0]));  // open: nQ
  LAB_8_ES_3_LATCH_D_main main_2 (.D(INPUT[1]), .Clock(and_1_out), .Q(OUTPUT[1]));  // open: nQ
  LAB_8_ES_3_LATCH_D_main main_3 (.D(INPUT[2]), .Clock(and_1_out), .Q(OUTPUT[2]));  // open: nQ
  LAB_8_ES_3_LATCH_D_main main_4 (.D(INPUT[3]), .Clock(and_1_out), .Q(OUTPUT[3]));  // open: nQ
endmodule
