// Logisim project LAB 8 ES 5 RESET.circ as structural Verilog: 1 circuit, main circuit main
module main (
  input  [3:0] INPUT,
  input  WRITE,
  input  RESET,
  output [3:0] OUTPUT
);

  wire CLK_out, or_1_out;
  wire [3:0] and_1_out;

  Clock CLK (.out(CLK_out));
  assign and_1_out = INPUT & ~{4{RESET}};  // AND_Gate and_1, 4 bits wide
  or or_1 (or_1_out, WRITE, RESET);
  LAB_8_ES_4_MEMORIZZAZIONE_4_BIT_main main_1 (.INPUT(and_1_out), .CLK(CLK_out), .WRITE(or_1_out), .OUTPUT(OUTPUT));
endmodule
