// Logisim project LAB 8 ES 6 FLIP FLOP.circ as structural Verilog: 1 circuit, main circuit FLIP FLOP
module FLIP_FLOP (
  input  D,
  input  CLOCK,
  output out_3
);

  wire main_1_q, not_1_out;

  LAB_8_ES_3_LATCH_D_main main_1 (.D(D), .Clock(CLOCK), .Q(main_1_q));  // open: nQ
  LAB_8_ES_3_LATCH_D_main main_2 (.D(main_1_q), .Clock(not_1_out), .Q(out_3));  // open: nQ
  not not_1 (not_1_out, CLOCK);
endmodule
