// Logisim project LAB 8 ES 6 SCORRIMENTO.circ as structural Verilog: 1 circuit, main circuit registro a scorrimento
module registro_a_scorrimento (
  input  b_t,
  input  clock,
  output [3:0] out_3
);

  FLIP_FLOP flip_flop_1 (.D(b_t), .CLOCK(clock), .out_3(out_3[0]));
  FLIP_FLOP flip_flop_2 (.D(out_3[1]), .CLOCK(clock), .out_3(out_3[2]));
  FLIP_FLOP flip_flop_3 (.D(out_3[0]), .CLOCK(clock), .out_3(out_3[1]));
  FLIP_FLOP flip_flop_4 (.D(out_3[2]), .CLOCK(clock), .out_3(out_3[3]));
endmodule
