// Logisim project LAB 9 ES 1.circ as structural Verilog: 3 circuits, main circuit OUTPUT
module OUTPUT (
  input  b0,
  input  b1,
  input  b2,
  output out_4
);

  wire and_1_out, and_2_out;

  and and_1 (and_1_out, ~b0, b1, ~b2);  // AND_Gate
  and and_2 (and_2_out, b0, ~b1, b2);  // AND_Gate
  or or_1 (out_4, and_1_out, and_2_out);
endmodule

module NEXT (
  input  X,
  input  b0,
  input  b1,
  input  b2,
  output b_prime_0,
  output b_prime_1,
  output b_prime_2
);


  assign b_prime_0 = X;
  assign b_prime_1 = b0;
  assign b_prime_2 = b1;
  // also tied to GND on the sheet: b2
endmodule

module MACCHINA_DI_MOORE (
  input  X,
  input  CLK,
  output out_3
);

  wire flip_flop_1_out_3, flip_flop_2_out_3, flip_flop_3_out_3, next_1_b_prime_0, next_1_b_prime_1,
       next_1_b_prime_2;

  FLIP_FLOP flip_flop_1 (.D(next_1_b_prime_0), .CLOCK(CLK), .out_3(flip_flop_1_out_3));
  // Probe on flip_flop_1_out_3
  // Probe on flip_flop_2_out_3
  FLIP_FLOP flip_flop_2 (.D(next_1_b_prime_1), .CLOCK(CLK), .out_3(flip_flop_2_out_3));
  // Probe on flip_flop_3_out_3
  FLIP_FLOP flip_flop_3 (.D(next_1_b_prime_2), .CLOCK(CLK), .out_3(flip_flop_3_out_3));
  OUTPUT output_1 (.b0(flip_flop_1_out_3), .b1(flip_flop_2_out_3), .b2(flip_flop_3_out_3), .out_4(out_3));
  NEXT next_1 (
    .X(X), .b0(flip_flop_1_out_3), .b1(flip_flop_2_out_3), .b2(flip_flop_3_out_3),
    .b_prime_0(next_1_b_prime_0), .b_prime_1(next_1_b_prime_1), .b_prime_2(next_1_b_prime_2));
endmodule
