// Logisim project LAB 9 ES 2 MSF MOORE.circ as structural Verilog: 4 circuits, main circuit output
module \output  (
  input  s,
  output \output 
);


  assign \output  = s;
endmodule

module next (
  input  s,
  input  r,
  input  a,
  input  b,
  output s_prime,
  output r_prime
);

  wire and_1_out, and_2_out, xor_2_out;

  xor xor_1 (s_prime, r, xor_2_out);
  xor xor_2 (xor_2_out, a, b);
  and and_1 (and_1_out, xor_2_out, r);
  and and_2 (and_2_out, a, b);
  or or_1 (r_prime, and_1_out, and_2_out);
  // also tied to GND on the sheet: s
endmodule

module sommatore_msf (
  input  clock,
  input  a,
  input  b,
  output \output 
);

  wire d_ff_1_q, d_ff_2_q, next_1_r_prime, next_1_s_prime;

  next next_1 (.r(d_ff_2_q), .a(a), .b(b), .s_prime(next_1_s_prime), .r_prime(next_1_r_prime));  // open: s
  D_Flip_Flop d_ff_1 (.clk(clock), .D(next_1_s_prime), .Q(d_ff_1_q));  // open: Qn, preset, en, reset
  D_Flip_Flop d_ff_2 (.clk(clock), .D(next_1_r_prime), .Q(d_ff_2_q));  // open: Qn, preset, en, reset
  \output  output_1 (.s(d_ff_1_q), .\output (\output ));
endmodule

module msf_moore (
  input  clk,
  input  [3:0] a,
  input  [3:0] b,
  output [3:0] out_4
);

  wire and_1_out, counter_1_carry, multiplexer_1_out, multiplexer_2_out, write_out;
  wire [2:0] counter_1_q;

  Button write (.out(write_out));
  Counter #(.width(3), .max('h4), .trigger("falling")) counter_1 (
    .Q(counter_1_q), .carry(counter_1_carry), .clk(and_1_out), .clr(write_out));  // open: load, D, count
  and and_1 (and_1_out, ~counter_1_carry, clk);  // AND_Gate
  // Probe on counter_1_q
  Multiplexer #(.select(3), .enable("false")) multiplexer_1 (
    .in0(a[0]), .in1(a[1]), .in2(a[2]), .in3(a[3]), .out(multiplexer_1_out), .sel(counter_1_q));  // open: in4, in5, in6, in7
  Multiplexer #(.select(3), .enable("false")) multiplexer_2 (
    .in0(b[0]), .in1(b[1]), .in2(b[2]), .in3(b[3]), .out(multiplexer_2_out), .sel(counter_1_q));  // open: in4, in5, in6, in7
  sommatore_msf sommatore_msf_1 (.clock(and_1_out), .a(multiplexer_1_out), .b(multiplexer_2_out), .\output (out_4[3]));
  D_Flip_Flop d_ff_1 (.clk(and_1_out), .D(out_4[2]), .Q(out_4[1]));  // open: Qn, preset, en, reset
  D_Flip_Flop d_ff_2 (.clk(and_1_out), .D(out_4[3]), .Q(out_4[2]));  // open: Qn, preset, en, reset
  D_Flip_Flop d_ff_3 (.clk(and_1_out), .D(out_4[1]), .Q(out_4[0]));  // open: Qn, preset, en, reset
endmodule
