// Logisim project LAB 9 ES 7 MEMORIA 4 BIT.circ as structural Verilog: 1 circuit, main circuit main
module main (
  input  [3:0] PAROLA,
  input  b_t,
  input  CLK,
  input  W,
  input  R,
  input  S,
  output [3:0] out_7
);

  wire and_1_out, and_2_out, and_3_out, and_4_out, and_5_out, multiplexer_1_out, multiplexer_2_out,
       multiplexer_3_out, multiplexer_4_out, not_1_out, not_2_out, or_1_out, undriven;

  or or_1 (or_1_out, W, R, S);
  not not_1 (not_1_out, R);
  not not_2 (not_2_out, S);
  and and_1 (and_1_out, CLK, or_1_out);
  and and_2 (and_2_out, not_1_out, PAROLA[0]);
  Multiplexer multiplexer_1 (.in0(b_t), .in1(and_2_out), .out(multiplexer_1_out), .sel(not_2_out), .en(undriven));
  Multiplexer multiplexer_2 (.in0(b_t), .in1(and_4_out), .out(multiplexer_2_out), .sel(not_2_out));  // open: en
  FLIP_FLOP flip_flop_1 (.D(multiplexer_1_out), .CLOCK(and_1_out), .out_3(out_7[0]));
  and and_3 (and_3_out, not_1_out, PAROLA[2]);
  and and_4 (and_4_out, not_1_out, PAROLA[1]);
  Multiplexer multiplexer_3 (.in0(b_t), .in1(and_3_out), .out(multiplexer_3_out), .sel(not_2_out));  // open: en
  FLIP_FLOP flip_flop_2 (.D(multiplexer_2_out), .CLOCK(and_1_out), .out_3(out_7[1]));
  and and_5 (and_5_out, not_1_out, PAROLA[3]);
  Multiplexer multiplexer_4 (.in0(b_t), .in1(and_5_out), .out(multiplexer_4_out), .sel(not_2_out));  // open: en
  FLIP_FLOP flip_flop_3 (.D(multiplexer_4_out), .CLOCK(and_1_out), .out_3(out_7[3]));
  FLIP_FLOP flip_flop_4 (.D(multiplexer_3_out), .CLOCK(and_1_out), .out_3(out_7[2]));
endmodule
