// Logisim project LAB 9 ES 8 - 4 PAROLE 4 BIT.circ as structural Verilog: 2 circuits, main circuit 4 BIT
module _4_BIT (
  input  CLK,
  input  [3:0] WORD,
  output out_0,
  output out_1,
  output out_2,
  output out_3
);

  LAB_8_ES_3_LATCH_D_main main_1 (.D(WORD[0]), .Clock(CLK), .Q(out_0));  // open: nQ
  LAB_8_ES_3_LATCH_D_main main_2 (.D(WORD[1]), .Clock(CLK), .Q(out_1));  // open: nQ
  LAB_8_ES_3_LATCH_D_main main_3 (.D(WORD[2]), .Clock(CLK), .Q(out_2));  // open: nQ
  LAB_8_ES_3_LATCH_D_main main_4 (.D(WORD[3]), .Clock(CLK), .Q(out_3));  // open: nQ
endmodule

module _4_PAROLE (
  input  in_1,
  input  [3:0] WORD,
  input  [1:0] ADDRESS,
  output [15:0] out_4
);

  wire [3:0] demultiplexer_1_out0, demultiplexer_1_out1, demultiplexer_1_out2, demultiplexer_1_out3;

  Demultiplexer #(.select(2), .width(4)) demultiplexer_1 (
    .out0(demultiplexer_1_out0), .out1(demultiplexer_1_out1), .out2(demultiplexer_1_out2),
    .out3(demultiplexer_1_out3), .in(WORD), .sel(ADDRESS));  // open: en
  _4_BIT u_4_bit_1 (
    .CLK(in_1), .WORD(demultiplexer_1_out0), .out_0(out_4[0]), .out_1(out_4[1]), .out_2(out_4[2]),
    .out_3(out_4[3]));
  _4_BIT u_4_bit_2 (
    .CLK(in_1), .WORD(demultiplexer_1_out1), .out_0(out_4[4]), .out_1(out_4[5]), .out_2(out_4[6]),
    .out_3(out_4[7]));
  _4_BIT u_4_bit_3 (
    .CLK(in_1), .WORD(demultiplexer_1_out2), .out_0(out_4[8]), .out_1(out_4[9]), .out_2(out_4[10]),
    .out_3(out_4[11]));
  _4_BIT u_4_bit_4 (
    .CLK(in_1), .WORD(demultiplexer_1_out3), .out_0(out_4[12]), .out_1(out_4[13]), .out_2(out_4[14]),
    .out_3(out_4[15]));
endmodule
