// Logisim project Progetto Netflix - Malune.circ as structural Verilog: 12 circuits, main circuit main: NETFLIX
module main__NETFLIX (
  input  pausa,
  output [3:0] out_2,
  output [3:0] out_3,
  output [3:0] out_4
);

  wire Black_Mirror, Bojack_Horseman, Breaking_Bad, cancella, clock, invio, La_casa_di_carta,
       La_regina_degli_scacchi, Narcos, Orange_is_the_new_black, risultati, Stranger_Things, The_Crown,
       The_social_dilemma, y_n;
  wire [3:0] film_selezionato;
  wire [6:0] ascii1, ascii2, led_matrix_1_c0, led_matrix_1_c1, led_matrix_1_c2, led_matrix_1_c3,
       led_matrix_1_c4, led_matrix_1_c5, led_matrix_1_c6, led_matrix_1_c7, led_matrix_1_c8, led_matrix_1_c9,
       led_matrix_1_c10, led_matrix_1_c11, led_matrix_1_c12, led_matrix_1_c13, led_matrix_1_c14,
       led_matrix_1_c15, led_matrix_1_c16, led_matrix_1_c17, led_matrix_1_c18, led_matrix_1_c19,
       led_matrix_1_c20, led_matrix_1_c21, led_matrix_1_c22, led_matrix_1_c23, led_matrix_1_c24,
       led_matrix_1_c25, led_matrix_1_c26, led_matrix_1_c27, led_matrix_1_c28;

  Button _1 (.out(La_casa_di_carta));
  Button _2 (.out(The_social_dilemma));
  Button _3 (.out(Black_Mirror));
  Button _4 (.out(Narcos));
  Button _5 (.out(Bojack_Horseman));
  Clock clock_1 (.out(clock));
  selezione_utente selezione_utente_1 (
    ._0(La_casa_di_carta), ._1(The_social_dilemma), ._2(Black_Mirror), ._3(Narcos), ._4(Bojack_Horseman),
    ._5(The_Crown), ._6(Stranger_Things), ._7(Breaking_Bad), ._8(Orange_is_the_new_black),
    ._9(La_regina_degli_scacchi), .reset(cancella), .film_selezionato(film_selezionato), .clock(clock),
    .y_n(y_n));
  Button _6 (.out(The_Crown));
  Button _7 (.out(Stranger_Things));
  Button _8 (.out(Breaking_Bad));
  Button _9 (.out(Orange_is_the_new_black));
  Button _10 (.out(La_regina_degli_scacchi));
  LED_Matrix led_matrix_1 (
    .c0(led_matrix_1_c0), .c1(led_matrix_1_c1), .c2(led_matrix_1_c2), .c3(led_matrix_1_c3),
    .c4(led_matrix_1_c4), .c5(led_matrix_1_c5), .c9(led_matrix_1_c9), .c13(led_matrix_1_c13),
    .c17(led_matrix_1_c17), .c20(led_matrix_1_c20), .c22(led_matrix_1_c22), .c28(led_matrix_1_c28),
    .c6(led_matrix_1_c6), .c7(led_matrix_1_c7), .c8(led_matrix_1_c8), .c10(led_matrix_1_c10),
    .c12(led_matrix_1_c12), .c11(led_matrix_1_c11), .c14(led_matrix_1_c14), .c15(led_matrix_1_c15),
    .c16(led_matrix_1_c16), .c18(led_matrix_1_c18), .c19(led_matrix_1_c19), .c21(led_matrix_1_c21),
    .c23(led_matrix_1_c23), .c24(led_matrix_1_c24), .c25(led_matrix_1_c25), .c26(led_matrix_1_c26),
    .c27(led_matrix_1_c27), .pausa(pausa), .clock(clock));
  DotMatrix #(.matrixcols(29)) dotmatrix_1 (
    .col0(led_matrix_1_c0), .col1(led_matrix_1_c1), .col2(led_matrix_1_c2), .col3(led_matrix_1_c3),
    .col4(led_matrix_1_c4), .col5(led_matrix_1_c5), .col6(led_matrix_1_c6), .col7(led_matrix_1_c7),
    .col8(led_matrix_1_c8), .col9(led_matrix_1_c9), .col10(led_matrix_1_c10), .col11(led_matrix_1_c11),
    .col12(led_matrix_1_c12), .col13(led_matrix_1_c13), .col14(led_matrix_1_c14), .col15(led_matrix_1_c15),
    .col16(led_matrix_1_c16), .col17(led_matrix_1_c17), .col18(led_matrix_1_c18), .col19(led_matrix_1_c19),
    .col20(led_matrix_1_c20), .col21(led_matrix_1_c21), .col22(led_matrix_1_c22), .col23(led_matrix_1_c23),
    .col24(led_matrix_1_c24), .col25(led_matrix_1_c25), .col26(led_matrix_1_c26), .col27(led_matrix_1_c27),
    .col28(led_matrix_1_c28));
  TTY_selezione_utente tty_selezione_utente_1 (
    .y_n(y_n), .clock(clock), .cancella(cancella), .film_selezionato(film_selezionato), .ascii(ascii1));
  TTY #(.rows(2)) tty_1 (.data(ascii1), .clk(clock), .we(y_n), .clr(cancella));
  TTY #(.rows(6)) tty_2 (.data(ascii2), .clk(clock), .we(risultati), .clr(cancella));
  Button button_1 (.out(invio));
  calcolatore_scelti_per_te calcolatore_scelti_per_te_1 (
    .film_selezionato(film_selezionato), .invio(invio), .clock(clock), .cancella(cancella),
    .first_film(out_2), .second_film(out_3), .third_film(out_4), .fine_conteggi(risultati));
  Button button_2 (.out(cancella));
  TTY_scelti_per_te tty_scelti_per_te_1 (
    .risultati(risultati), .clock(clock), .first_f(out_2), .second_f(out_3), .third_f(out_4),
    .cancella(cancella), .ascii(ascii2));

  // Notes on the sheet:
  //   Selezione titolo
  //   Seleziona un titolo che ti è piaciuto:
  //   Titolo selezionato:
  //   Scelti per te:
endmodule

module LED_Matrix (
  input  clock,
  input  pausa,
  output [6:0] c0,
  output [6:0] c1,
  output [6:0] c2,
  output [6:0] c3,
  output [6:0] c4,
  output [6:0] c5,
  output [6:0] c6,
  output [6:0] c7,
  output [6:0] c8,
  output [6:0] c9,
  output [6:0] c10,
  output [6:0] c11,
  output [6:0] c12,
  output [6:0] c13,
  output [6:0] c14,
  output [6:0] c15,
  output [6:0] c16,
  output [6:0] c17,
  output [6:0] c18,
  output [6:0] c19,
  output [6:0] c20,
  output [6:0] c21,
  output [6:0] c22,
  output [6:0] c23,
  output [6:0] c24,
  output [6:0] c25,
  output [6:0] c26,
  output [6:0] c27,
  output [6:0] c28
);

  wire and_1_out, and_4_out, and_6_out, and_7_out, and_9_out, and_12_out, and_17_out, and_19_out, and_22_out,
       and_24_out, counter_1_carry, counter_2_carry, counter_3_carry, counter_4_carry, counter_5_carry,
       counter_7_carry, counter_9_carry, counter_11_carry, counter_13_carry, counter_14_carry,
       counter_15_carry, counter_16_carry, counter_18_carry, counter_21_carry, replay;
  wire [0:0] counter_13_q;
  wire [1:0] counter_1_q, counter_4_q, counter_5_q, counter_6_q, counter_9_q, counter_10_q, counter_11_q,
       counter_12_q, counter_14_q, counter_16_q, counter_17_q, counter_19_q, counter_21_q;
  wire [2:0] counter_7_q, counter_18_q, counter_20_q;

  and and_1 (and_1_out, clock, ~pausa);  // AND_Gate
  Counter #(.width(3), .max('h5), .ongoal("stay")) counter_1 (
    .Q({c1[4], counter_1_q}), .carry(counter_1_carry), .clk(and_1_out), .clr(replay));  // open: load, D, count
  Counter #(.width(1), .max('h1), .ongoal("stay")) counter_2 (
    .count(counter_1_carry), .Q(c2[4]), .carry(counter_2_carry), .clk(and_1_out), .clr(replay));  // open: load, D
  Counter #(.width(1), .max('h1), .ongoal("stay")) counter_3 (
    .count(counter_2_carry), .Q(c3[3]), .carry(counter_3_carry), .clk(and_1_out), .clr(replay));  // open: load, D
  Counter #(.width(3), .max('h5), .ongoal("stay")) counter_4 (
    .count(counter_3_carry), .Q({c4[4], counter_4_q}), .carry(counter_4_carry), .clk(and_1_out), .clr(replay));  // open: load, D
  Counter #(.width(3), .max('h5), .ongoal("stay")) counter_5 (
    .count(counter_4_carry), .Q({c6[2], counter_5_q}), .carry(counter_5_carry), .clk(and_1_out), .clr(replay));  // open: load, D
  Counter #(.width(3), .max('h5), .ongoal("stay")) counter_6 (
    .count(counter_5_carry), .Q({c7[5], counter_6_q}), .clk(and_1_out), .clr(replay));  // open: load, D, carry
  Counter #(.width(3), .max('h5), .ongoal("stay")) counter_7 (
    .count(counter_5_carry), .Q(counter_7_q), .carry(counter_7_carry), .clk(and_1_out), .clr(replay));  // open: load, D
  Counter #(.width(1), .max('h1), .ongoal("stay")) counter_8 (
    .count(counter_7_carry), .Q(c10[5]), .clk(and_1_out), .clr(replay));  // open: load, D, carry
  Counter #(.width(3), .max('h7), .ongoal("stay")) counter_9 (
    .count(counter_7_carry), .Q({c11[4], counter_9_q}), .carry(counter_9_carry), .clk(and_1_out), .clr(replay));  // open: load, D
  Counter #(.width(2), .max('h3), .ongoal("stay")) counter_10 (
    .count(counter_7_carry), .Q(counter_10_q), .clk(and_1_out), .clr(replay));  // open: load, D, carry
  Counter #(.width(3), .max('h5), .ongoal("stay")) counter_11 (
    .count(counter_9_carry), .Q({c14[4], counter_11_q}), .carry(counter_11_carry), .clk(and_1_out),
    .clr(replay));  // open: load, D
  Counter #(.width(2), .max('h3), .ongoal("stay")) counter_12 (
    .count(counter_11_carry), .Q(counter_12_q), .clk(and_1_out), .clr(replay));  // open: load, D, carry
  Counter #(.width(2), .max('h3), .ongoal("stay")) counter_13 (
    .count(counter_11_carry), .Q({c16[5], counter_13_q[0]}), .carry(counter_13_carry), .clk(and_1_out),
    .clr(replay));  // open: load, D
  Counter #(.width(3), .max('h5), .ongoal("stay")) counter_14 (
    .count(counter_13_carry), .Q({c18[2], counter_14_q}), .carry(counter_14_carry), .clk(and_1_out),
    .clr(replay));  // open: load, D
  Counter #(.width(1), .max('h1), .ongoal("stay")) counter_15 (
    .count(counter_14_carry), .Q(c19[1]), .carry(counter_15_carry), .clk(and_1_out), .clr(replay));  // open: load, D
  Counter #(.width(3), .max('h5), .ongoal("stay")) counter_16 (
    .count(counter_15_carry), .Q({c21[4], counter_16_q}), .carry(counter_16_carry), .clk(and_1_out),
    .clr(replay));  // open: load, D
  Counter #(.width(3), .max('h5), .ongoal("stay")) counter_17 (
    .count(counter_16_carry), .Q({c23[5], counter_17_q}), .clk(and_1_out), .clr(replay));  // open: load, D, carry
  Counter #(.width(3), .max('h5), .ongoal("stay")) counter_18 (
    .count(counter_16_carry), .Q(counter_18_q), .carry(counter_18_carry), .clk(and_1_out), .clr(replay));  // open: load, D
  Counter #(.width(2), .max('h3), .ongoal("stay")) counter_19 (
    .count(counter_16_carry), .Q(counter_19_q), .clk(and_1_out), .clr(replay));  // open: load, D, carry
  Counter #(.width(3), .max('h4), .ongoal("stay")) counter_20 (
    .count(counter_18_carry), .Q(counter_20_q), .clk(and_1_out), .clr(replay));  // open: load, D, carry
  Counter #(.width(3), .max('h4), .ongoal("stay")) counter_21 (
    .count(counter_18_carry), .Q({c27[5], counter_21_q}), .carry(counter_21_carry), .clk(and_1_out),
    .clr(replay));  // open: load, D
  Counter #(.width(3), .max('h7), .ongoal("stay")) counter_22 (
    .count(counter_21_carry), .carry(replay), .clk(and_1_out), .clr(replay));  // open: load, D, Q
  and and_2 (c25[3], counter_19_q[0], counter_19_q[1]);
  and and_3 (c1[5], c1[4], counter_1_q[0]);
  and and_4 (and_4_out, counter_1_q[1], counter_1_q[0]);
  or or_1 (c1[2], counter_1_q[1], c1[4]);
  or or_2 (c1[1], counter_1_q[0], counter_1_q[1], c1[4]);
  and and_5 (c4[5], c4[4], counter_4_q[0]);
  and and_6 (and_6_out, counter_4_q[1], counter_4_q[0]);
  or or_3 (c4[3], and_6_out, c4[4]);
  or or_4 (c4[2], counter_4_q[1], c4[4]);
  or or_5 (c4[1], counter_4_q[0], counter_4_q[1], c4[4]);
  or or_6 (c6[5], c6[2], counter_5_q[1], counter_5_q[0]);
  or or_7 (c6[4], counter_5_q[1], c6[2]);
  and and_7 (and_7_out, counter_5_q[1], counter_5_q[0]);
  or or_8 (c6[3], and_7_out, c6[2]);
  and and_8 (c6[1], c6[2], counter_5_q[0]);
  and and_9 (and_9_out, counter_6_q[1], counter_6_q[0]);
  or or_9 (c7[1], counter_6_q[0], counter_6_q[1], c7[5]);
  and and_10 (c8[5], counter_7_q[2], counter_7_q[0]);
  and and_11 (c8[3], counter_7_q[2], counter_7_q[1]);
  or or_10 (c8[1], counter_7_q[1], counter_7_q[2]);
  or or_11 (c11[5], c11[4], counter_9_q[1]);
  and and_12 (and_12_out, c11[4], counter_9_q[0]);
  and and_13 (c11[2], c11[4], counter_9_q[1]);
  and and_14 (c11[1], c11[4], counter_9_q[1], counter_9_q[0]);
  and and_15 (c12[5], counter_10_q[0], counter_10_q[1]);
  and and_16 (c14[5], c14[4], counter_11_q[0]);
  and and_17 (and_17_out, counter_11_q[1], counter_11_q[0]);
  or or_12 (c14[2], counter_11_q[1], c14[4]);
  or or_13 (c14[1], counter_11_q[0], counter_11_q[1], c14[4]);
  or or_14 (c15[5], counter_12_q[0], counter_12_q[1]);
  and and_18 (c15[3], counter_12_q[0], counter_12_q[1]);
  or or_15 (c18[5], c18[2], counter_14_q[1], counter_14_q[0]);
  or or_16 (c18[4], counter_14_q[1], c18[2]);
  and and_19 (and_19_out, counter_14_q[1], counter_14_q[0]);
  or or_17 (c18[3], and_19_out, c18[2]);
  and and_20 (c18[1], c18[2], counter_14_q[0]);
  and and_21 (c21[5], c21[4], counter_16_q[0]);
  and and_22 (and_22_out, counter_16_q[1], counter_16_q[0]);
  or or_18 (c21[2], counter_16_q[1], c21[4]);
  or or_19 (c21[1], counter_16_q[0], counter_16_q[1], c21[4]);
  or or_20 (c23[1], c23[5], counter_17_q[1], counter_17_q[0]);
  and and_23 (c24[4], counter_18_q[2], counter_18_q[0]);
  or or_21 (c24[2], counter_18_q[2], counter_18_q[1]);
  and and_24 (and_24_out, counter_20_q[1], counter_20_q[0]);
  or or_22 (c26[2], counter_20_q[2], counter_20_q[0], counter_20_q[1]);
  or or_23 (c27[1], c27[5], counter_21_q[1]);
  or or_24 (c1[3], and_4_out, c1[4]);
  or or_25 (c7[3], and_9_out, c7[5]);
  or or_26 (c11[3], and_12_out, c11[2]);
  or or_27 (c14[3], and_17_out, c14[4]);
  or or_28 (c21[3], and_22_out, c21[4]);
  or or_29 (c26[4], counter_20_q[2], and_24_out);

  assign c0 = {7{1'b0}};
  assign {c1[6], c1[0]} = 2'b00;
  assign {c2[6:5], c2[3:0]} = {6{1'b0}};
  assign {c3[6:4], c3[2:0]} = {6{1'b0}};
  assign {c4[6], c4[0]} = 2'b00;
  assign c5 = {7{1'b0}};
  assign {c6[6], c6[0]} = 2'b00;
  assign {c7[6], c7[4], c7[2], c7[0]} = 4'b0000;
  assign {c8[6], c8[4], c8[2], c8[0]} = 4'b0000;
  assign c9 = {7{1'b0}};
  assign {c10[6], c10[4:0]} = {6{1'b0}};
  assign {c11[6], c11[0]} = 2'b00;
  assign {c12[6], c12[4:0]} = {6{1'b0}};
  assign c13 = {7{1'b0}};
  assign {c14[6], c14[0]} = 2'b00;
  assign {c15[6], c15[4], c15[2:0]} = {5{1'b0}};
  assign {c16[6], c16[4:0]} = {6{1'b0}};
  assign c17 = {7{1'b0}};
  assign {c18[6], c18[0]} = 2'b00;
  assign {c19[6:2], c19[0]} = {6{1'b0}};
  assign c20 = {7{1'b0}};
  assign {c21[6], c21[0]} = 2'b00;
  assign c22 = {7{1'b0}};
  assign {c23[6], c23[4:2], c23[0]} = {5{1'b0}};
  assign {c24[6:5], c24[3], c24[1:0]} = {5{1'b0}};
  assign {c25[6:4], c25[2:0]} = {6{1'b0}};
  assign {c26[6:5], c26[3], c26[1:0]} = {5{1'b0}};
  assign {c27[6], c27[4:2], c27[0]} = {5{1'b0}};
  assign c28 = {7{1'b0}};
  // also tied to GND on the sheet: {counter_13_q[0], counter_21_q[0]}
endmodule

module selezione_utente (
  input  _0,
  input  _1,
  input  _2,
  input  _3,
  input  _4,
  input  _5,
  input  _6,
  input  _7,
  input  _8,
  input  _9,
  input  clock,
  input  reset,
  output [3:0] film_selezionato,
  output y_n
);

  wire or_1_out;
  wire [3:0] priority_encoder_1_p9;

  or or_1 (or_1_out, _0, _1, _2, _3, _4, _5, _6, _7, _8, _9);
  // Priority_Encoder #(.select(4)) priority_encoder_1: pin names not known; wires that end beside it: _0, _1, _2, _3, _4, _5, _6, _7, priority_encoder_1_p9, _8, _9
  D_Flip_Flop #(.trigger("falling")) d_ff_1 (
    .clk(clock), .D(priority_encoder_1_p9[3]), .Q(film_selezionato[3]));  // open: Qn, preset, en, reset
  D_Flip_Flop d_ff_2 (
    .clk(clock), .D(priority_encoder_1_p9[2]), .Q(film_selezionato[2]));  // open: Qn, preset, en, reset
  D_Flip_Flop d_ff_3 (
    .clk(clock), .D(priority_encoder_1_p9[1]), .Q(film_selezionato[1]));  // open: Qn, preset, en, reset
  D_Flip_Flop d_ff_4 (
    .clk(clock), .D(priority_encoder_1_p9[0]), .Q(film_selezionato[0]));  // open: Qn, preset, en, reset
  S_R_Flip_Flop s_r_ff_1 (.S(or_1_out), .clk(clock), .R(reset), .Q(y_n));  // open: Qn, preset, reset, en
endmodule

module TTY_selezione_utente (
  input  y_n,
  input  clock,
  input  cancella,
  input  [3:0] film_selezionato,
  output [6:0] ascii
);

  wire and_1_out, nand_1_out;
  wire [4:0] counter_1_q;

  and and_1 (and_1_out, y_n, ~clock);  // AND_Gate
  Counter #(.width(5), .max('h1c), .ongoal("stay"), .trigger("falling")) counter_1 (
    .count(nand_1_out), .Q(counter_1_q), .clk(and_1_out), .clr(cancella));  // open: load, D, carry
  nand nand_1 (nand_1_out, ascii[0], ascii[1], ascii[2], ascii[3], ascii[4], ascii[5], ascii[6]);
  ROM_ascii rom_ascii_1 (.char(counter_1_q), .titolo(film_selezionato), .ascii(ascii));

  // Notes on the sheet:
  //   stop a fine stringa
endmodule

module ROM_ascii (
  input  [4:0] char,
  input  [3:0] titolo,
  output [6:0] ascii
);

  ROM #(.addrWidth(9), .dataWidth(7)) rom_1 (.addr({titolo, char}), .data(ascii));  // open: sel

  // Notes on the sheet:
  //   titoli ascii
  //   contents of rom_1 (hex, n*v repeats v):
  //   31 2e 20 4c 61 20 63 61 73 61 20 64 69 20 63 61 72 74 61 a 12*0 32 2e 20 54 68 65 20 73 6f 63 69 61
  //   6c 20 64 69 6c 65 6d 6d 61 a 10*0 33 2e 20 42 6c 61 63 6b 20 6d 69 72 72 6f 72 a 16*0 34 2e 20 4e 61
  //   72 63 6f 73 a 22*0 35 2e 20 42 6f 6a 61 63 6b 20 48 6f 72 73 65 6d 61 6e a 13*0 36 2e 20 54 68 65 20
  //   43 72 6f 77 6e a 19*0 37 2e 20 53 74 72 61 6e 67 65 72 20 54 68 69 6e 67 73 a 13*0 38 2e 20 42 72 65
  //   61 6b 69 6e 67 20 42 61 64 a 16*0 39 2e 20 4f 72 61 6e 67 65 20 69 73 20 74 68 65 20 6e 65 77 20 62
  //   6c 61 63 6b a 5*0 31 30 2e 20 4c 61 20 72 65 67 69 6e 61 20 64 65 67 6c 69 20 73 63 61 63 63 68 69 a
endmodule

module calcolatore_scelti_per_te (
  input  [3:0] film_selezionato,
  input  invio,
  input  clock,
  input  cancella,
  output fine_conteggi,
  output [3:0] first_film,
  output [3:0] second_film,
  output [3:0] third_film
);

  wire and_1_out, and_2_out, and_3_out, rom_opinioni_1_piace, rom_opinioni_2_piace, rom_opinioni_3_piace,
       rom_opinioni_4_piace, rom_opinioni_5_piace, rom_opinioni_6_piace, rom_opinioni_7_piace,
       rom_opinioni_8_piace, rom_opinioni_9_piace, rom_opinioni_10_piace, rom_opinioni_11_piace, s_r_ff_1_q;
  wire [3:0] _0y, _1y, _2y, _3y, _4y, _5y, _6y, _7y, _8y, _9y, calcolatore_classifica_1_other_film,
       calcolatore_classifica_1_other_film_2, calcolatore_classifica_1_other_film_3,
       calcolatore_classifica_1_other_film_4, calcolatore_classifica_1_other_film_5,
       calcolatore_classifica_1_other_film_6, calcolatore_classifica_1_other_film_7,
       calcolatore_classifica_1_other_film_8, calcolatore_classifica_1_other_film_9,
       calcolatore_classifica_2_other_film, calcolatore_classifica_2_other_film_2,
       calcolatore_classifica_2_other_film_3, calcolatore_classifica_2_other_film_4,
       calcolatore_classifica_2_other_film_5, calcolatore_classifica_2_other_film_6,
       calcolatore_classifica_2_other_film_7, calcolatore_classifica_2_other_film_8,
       calcolatore_classifica_2_other_film_9, filtro_pre_classifica_1_film, filtro_pre_classifica_1_film_0_2,
       filtro_pre_classifica_1_film_10, filtro_pre_classifica_1_film_11, filtro_pre_classifica_1_film_12,
       filtro_pre_classifica_1_film_13, filtro_pre_classifica_1_film_14, filtro_pre_classifica_1_film_15,
       filtro_pre_classifica_1_film_16, filtro_pre_classifica_1_film_17, filtro_pre_classifica_2_film,
       filtro_pre_classifica_2_film_0_2, filtro_pre_classifica_2_film_10, filtro_pre_classifica_2_film_11,
       filtro_pre_classifica_2_film_12, filtro_pre_classifica_2_film_13, filtro_pre_classifica_2_film_14,
       filtro_pre_classifica_2_film_15, filtro_pre_classifica_2_film_16, filtro_pre_classifica_2_film_17,
       filtro_pre_classifica_3_film, filtro_pre_classifica_3_film_0_2, filtro_pre_classifica_3_film_10,
       filtro_pre_classifica_3_film_11, filtro_pre_classifica_3_film_12, filtro_pre_classifica_3_film_13,
       filtro_pre_classifica_3_film_14, filtro_pre_classifica_3_film_15, filtro_pre_classifica_3_film_16,
       filtro_pre_classifica_3_film_17, persona_q, tot;
  wire [6:0] _0, _1, _2, _3, _4, _5, _6, _7, _8, _9, calcolatore_classifica_1_first,
       calcolatore_classifica_1_other, calcolatore_classifica_1_other_2, calcolatore_classifica_1_other_3,
       calcolatore_classifica_1_other_4, calcolatore_classifica_1_other_5, calcolatore_classifica_1_other_6,
       calcolatore_classifica_1_other_7, calcolatore_classifica_1_other_8, calcolatore_classifica_1_other_9,
       calcolatore_classifica_2_first, calcolatore_classifica_2_other, calcolatore_classifica_2_other_2,
       calcolatore_classifica_2_other_3, calcolatore_classifica_2_other_4, calcolatore_classifica_2_other_5,
       calcolatore_classifica_2_other_6, calcolatore_classifica_2_other_7, calcolatore_classifica_2_other_8,
       calcolatore_classifica_2_other_9, filtro_pre_classifica_1__0_2, filtro_pre_classifica_1_out_24,
       filtro_pre_classifica_1_out_26, filtro_pre_classifica_1_out_28, filtro_pre_classifica_1_out_30,
       filtro_pre_classifica_1_out_32, filtro_pre_classifica_1_out_34, filtro_pre_classifica_1_out_36,
       filtro_pre_classifica_1_out_38, filtro_pre_classifica_1_out_40, filtro_pre_classifica_2__0_2,
       filtro_pre_classifica_2_out_24, filtro_pre_classifica_2_out_26, filtro_pre_classifica_2_out_28,
       filtro_pre_classifica_2_out_30, filtro_pre_classifica_2_out_32, filtro_pre_classifica_2_out_34,
       filtro_pre_classifica_2_out_36, filtro_pre_classifica_2_out_38, filtro_pre_classifica_2_out_40,
       filtro_pre_classifica_3__0_2, filtro_pre_classifica_3_out_24, filtro_pre_classifica_3_out_26,
       filtro_pre_classifica_3_out_28, filtro_pre_classifica_3_out_30, filtro_pre_classifica_3_out_32,
       filtro_pre_classifica_3_out_34, filtro_pre_classifica_3_out_36, filtro_pre_classifica_3_out_38,
       filtro_pre_classifica_3_out_40;

  S_R_Flip_Flop s_r_ff_1 (.S(invio), .clk(clock), .R(cancella), .Q(s_r_ff_1_q));  // open: Qn, preset, reset, en
  Counter #(.width(4), .max('ha), .ongoal("stay"), .trigger("falling")) persona (
    .Q(persona_q), .carry(fine_conteggi), .clk(and_1_out), .clr(cancella));  // open: load, D, count
  and and_1 (and_1_out, s_r_ff_1_q, clock);
  ROM_opinioni rom_opinioni_1 (.persona(persona_q), .film(4'b0000), .piace(rom_opinioni_1_piace));
  ROM_opinioni rom_opinioni_2 (.persona(persona_q), .film(4'b0001), .piace(rom_opinioni_2_piace));
  ROM_opinioni rom_opinioni_3 (.persona(persona_q), .film(4'b0010), .piace(rom_opinioni_3_piace));
  ROM_opinioni rom_opinioni_4 (.persona(persona_q), .film(4'b0011), .piace(rom_opinioni_4_piace));
  ROM_opinioni rom_opinioni_5 (.persona(persona_q), .film(4'b0100), .piace(rom_opinioni_5_piace));
  ROM_opinioni rom_opinioni_6 (.persona(persona_q), .film(4'b0101), .piace(rom_opinioni_6_piace));
  ROM_opinioni rom_opinioni_7 (.persona(persona_q), .film(4'b0110), .piace(rom_opinioni_7_piace));
  ROM_opinioni rom_opinioni_8 (.persona(persona_q), .film(4'b0111), .piace(rom_opinioni_8_piace));
  ROM_opinioni rom_opinioni_9 (.persona(persona_q), .film(4'b1000), .piace(rom_opinioni_9_piace));
  ROM_opinioni rom_opinioni_10 (.persona(persona_q), .film(4'b1001), .piace(rom_opinioni_10_piace));
  ROM_opinioni rom_opinioni_11 (.persona(persona_q), .film(film_selezionato), .piace(rom_opinioni_11_piace));
  and and_2 (and_2_out, ~fine_conteggi, rom_opinioni_11_piace);  // AND_Gate
  Counter #(.width(4), .max('hf), .ongoal("stay"), .trigger("falling")) counter_1 (
    .Q(tot), .clk(and_3_out), .clr(cancella));  // open: load, D, count, carry
  and and_3 (and_3_out, and_1_out, and_2_out);
  Counter #(.width(4), .max('hf), .ongoal("stay"), .trigger("falling")) counter_2 (
    .count(rom_opinioni_1_piace), .Q(_0y), .clk(and_3_out), .clr(cancella));  // open: load, D, carry
  Counter #(.width(4), .max('hf), .trigger("falling")) counter_3 (
    .count(rom_opinioni_2_piace), .Q(_1y), .clk(and_3_out), .clr(cancella));  // open: load, D, carry
  Counter #(.width(4), .max('hf), .trigger("falling")) counter_4 (
    .count(rom_opinioni_3_piace), .Q(_2y), .clk(and_3_out), .clr(cancella));  // open: load, D, carry
  Counter #(.width(4), .max('hf), .trigger("falling")) counter_5 (
    .count(rom_opinioni_4_piace), .Q(_3y), .clk(and_3_out), .clr(cancella));  // open: load, D, carry
  Counter #(.width(4), .max('hf), .trigger("falling")) counter_6 (
    .count(rom_opinioni_5_piace), .Q(_4y), .clk(and_3_out), .clr(cancella));  // open: load, D, carry
  Counter #(.width(4), .max('hf), .trigger("falling")) counter_7 (
    .count(rom_opinioni_6_piace), .Q(_5y), .clk(and_3_out), .clr(cancella));  // open: load, D, carry
  Counter #(.width(4), .max('hf), .trigger("falling")) counter_8 (
    .count(rom_opinioni_7_piace), .Q(_6y), .clk(and_3_out), .clr(cancella));  // open: load, D, carry
  Counter #(.width(4), .max('hf), .trigger("falling")) counter_9 (
    .count(rom_opinioni_8_piace), .Q(_7y), .clk(and_3_out), .clr(cancella));  // open: load, D, carry
  Counter #(.width(4), .max('hf), .trigger("falling")) counter_10 (
    .count(rom_opinioni_9_piace), .Q(_8y), .clk(and_3_out), .clr(cancella));  // open: load, D, carry
  Counter #(.width(4), .max('hf), .trigger("falling")) counter_11 (
    .count(rom_opinioni_10_piace), .Q(_9y), .clk(and_3_out), .clr(cancella));  // open: load, D, carry
  calcolatore_percentuali calcolatore_percentuali_1 (.yes(_0y), .tot(tot), .out_3(_0));
  calcolatore_percentuali calcolatore_percentuali_2 (.yes(_1y), .tot(tot), .out_3(_1));
  calcolatore_percentuali calcolatore_percentuali_3 (.yes(_2y), .tot(tot), .out_3(_2));
  calcolatore_percentuali calcolatore_percentuali_4 (.yes(_3y), .tot(tot), .out_3(_3));
  calcolatore_percentuali calcolatore_percentuali_5 (.yes(_4y), .tot(tot), .out_3(_4));
  calcolatore_percentuali calcolatore_percentuali_6 (.yes(_5y), .tot(tot), .out_3(_5));
  calcolatore_percentuali calcolatore_percentuali_7 (.yes(_6y), .tot(tot), .out_3(_6));
  calcolatore_percentuali calcolatore_percentuali_8 (.yes(_7y), .tot(tot), .out_3(_7));
  calcolatore_percentuali calcolatore_percentuali_9 (.yes(_8y), .tot(tot), .out_3(_8));
  calcolatore_percentuali calcolatore_percentuali_10 (.yes(_9y), .tot(tot), .out_3(_9));
  filtro_pre_classifica filtro_pre_classifica_1 (
    .film_da_scartare(film_selezionato), ._0(_0), .film_0(4'b0000), ._1(_1), .film_1(4'b0001), ._2(_2),
    .film_2(4'b0010), ._3(_3), .film_3(4'b0011), ._4(_4), .film_4(4'b0100), ._5(_5), .film_5(4'b0101),
    ._6(_6), .film_6(4'b0110), ._7(_7), .film_7(4'b0111), ._8(_8), .film_8(4'b1000), ._9(_9),
    .film_9(4'b1001), ._0_2(filtro_pre_classifica_1__0_2), .film_0_2(filtro_pre_classifica_1_film_0_2),
    .out_24(filtro_pre_classifica_1_out_24), .film(filtro_pre_classifica_1_film),
    .out_26(filtro_pre_classifica_1_out_26), .film_10(filtro_pre_classifica_1_film_10),
    .out_28(filtro_pre_classifica_1_out_28), .film_11(filtro_pre_classifica_1_film_11),
    .out_30(filtro_pre_classifica_1_out_30), .film_12(filtro_pre_classifica_1_film_12),
    .out_32(filtro_pre_classifica_1_out_32), .film_13(filtro_pre_classifica_1_film_13),
    .out_34(filtro_pre_classifica_1_out_34), .film_14(filtro_pre_classifica_1_film_14),
    .out_36(filtro_pre_classifica_1_out_36), .film_15(filtro_pre_classifica_1_film_15),
    .out_38(filtro_pre_classifica_1_out_38), .film_16(filtro_pre_classifica_1_film_16),
    .out_40(filtro_pre_classifica_1_out_40), .film_17(filtro_pre_classifica_1_film_17));
  calcolatore_classifica calcolatore_classifica_1 (
    ._0(filtro_pre_classifica_1__0_2), .film_0(filtro_pre_classifica_1_film_0_2),
    ._1(filtro_pre_classifica_1_out_24), .film_1(filtro_pre_classifica_1_film),
    ._2(filtro_pre_classifica_1_out_26), .film_2(filtro_pre_classifica_1_film_10),
    ._3(filtro_pre_classifica_1_out_28), .film_3(filtro_pre_classifica_1_film_11),
    ._4(filtro_pre_classifica_1_out_30), .film_4(filtro_pre_classifica_1_film_12),
    ._5(filtro_pre_classifica_1_out_32), .film_5(filtro_pre_classifica_1_film_13),
    ._6(filtro_pre_classifica_1_out_34), .film_6(filtro_pre_classifica_1_film_14),
    ._7(filtro_pre_classifica_1_out_36), .film_7(filtro_pre_classifica_1_film_15),
    ._8(filtro_pre_classifica_1_out_38), .film_8(filtro_pre_classifica_1_film_16),
    ._9(filtro_pre_classifica_1_out_40), .film_9(filtro_pre_classifica_1_film_17),
    .other(calcolatore_classifica_1_other), .other_film(calcolatore_classifica_1_other_film),
    .other_2(calcolatore_classifica_1_other_2), .other_film_2(calcolatore_classifica_1_other_film_2),
    .other_3(calcolatore_classifica_1_other_3), .other_film_3(calcolatore_classifica_1_other_film_3),
    .other_4(calcolatore_classifica_1_other_4), .other_film_4(calcolatore_classifica_1_other_film_4),
    .other_5(calcolatore_classifica_1_other_5), .other_film_5(calcolatore_classifica_1_other_film_5),
    .other_6(calcolatore_classifica_1_other_6), .other_film_6(calcolatore_classifica_1_other_film_6),
    .other_7(calcolatore_classifica_1_other_7), .other_film_7(calcolatore_classifica_1_other_film_7),
    .other_8(calcolatore_classifica_1_other_8), .other_film_8(calcolatore_classifica_1_other_film_8),
    .other_9(calcolatore_classifica_1_other_9), .other_film_9(calcolatore_classifica_1_other_film_9),
    .first(calcolatore_classifica_1_first), .first_film(first_film));
  filtro_pre_classifica filtro_pre_classifica_2 (
    .film_da_scartare(first_film), ._0(calcolatore_classifica_1_other),
    .film_0(calcolatore_classifica_1_other_film), ._1(calcolatore_classifica_1_other_2),
    .film_1(calcolatore_classifica_1_other_film_2), ._2(calcolatore_classifica_1_other_3),
    .film_2(calcolatore_classifica_1_other_film_3), ._3(calcolatore_classifica_1_other_4),
    .film_3(calcolatore_classifica_1_other_film_4), ._4(calcolatore_classifica_1_other_5),
    .film_4(calcolatore_classifica_1_other_film_5), ._5(calcolatore_classifica_1_other_6),
    .film_5(calcolatore_classifica_1_other_film_6), ._6(calcolatore_classifica_1_other_7),
    .film_6(calcolatore_classifica_1_other_film_7), ._7(calcolatore_classifica_1_other_8),
    .film_7(calcolatore_classifica_1_other_film_8), ._8(calcolatore_classifica_1_other_9),
    .film_8(calcolatore_classifica_1_other_film_9), ._9(calcolatore_classifica_1_first), .film_9(first_film),
    ._0_2(filtro_pre_classifica_2__0_2), .film_0_2(filtro_pre_classifica_2_film_0_2),
    .out_24(filtro_pre_classifica_2_out_24), .film(filtro_pre_classifica_2_film),
    .out_26(filtro_pre_classifica_2_out_26), .film_10(filtro_pre_classifica_2_film_10),
    .out_28(filtro_pre_classifica_2_out_28), .film_11(filtro_pre_classifica_2_film_11),
    .out_30(filtro_pre_classifica_2_out_30), .film_12(filtro_pre_classifica_2_film_12),
    .out_32(filtro_pre_classifica_2_out_32), .film_13(filtro_pre_classifica_2_film_13),
    .out_34(filtro_pre_classifica_2_out_34), .film_14(filtro_pre_classifica_2_film_14),
    .out_36(filtro_pre_classifica_2_out_36), .film_15(filtro_pre_classifica_2_film_15),
    .out_38(filtro_pre_classifica_2_out_38), .film_16(filtro_pre_classifica_2_film_16),
    .out_40(filtro_pre_classifica_2_out_40), .film_17(filtro_pre_classifica_2_film_17));
  calcolatore_classifica calcolatore_classifica_2 (
    ._0(filtro_pre_classifica_2__0_2), .film_0(filtro_pre_classifica_2_film_0_2),
    ._1(filtro_pre_classifica_2_out_24), .film_1(filtro_pre_classifica_2_film),
    ._2(filtro_pre_classifica_2_out_26), .film_2(filtro_pre_classifica_2_film_10),
    ._3(filtro_pre_classifica_2_out_28), .film_3(filtro_pre_classifica_2_film_11),
    ._4(filtro_pre_classifica_2_out_30), .film_4(filtro_pre_classifica_2_film_12),
    ._5(filtro_pre_classifica_2_out_32), .film_5(filtro_pre_classifica_2_film_13),
    ._6(filtro_pre_classifica_2_out_34), .film_6(filtro_pre_classifica_2_film_14),
    ._7(filtro_pre_classifica_2_out_36), .film_7(filtro_pre_classifica_2_film_15),
    ._8(filtro_pre_classifica_2_out_38), .film_8(filtro_pre_classifica_2_film_16),
    ._9(filtro_pre_classifica_2_out_40), .film_9(filtro_pre_classifica_2_film_17),
    .other(calcolatore_classifica_2_other), .other_film(calcolatore_classifica_2_other_film),
    .other_2(calcolatore_classifica_2_other_2), .other_film_2(calcolatore_classifica_2_other_film_2),
    .other_3(calcolatore_classifica_2_other_3), .other_film_3(calcolatore_classifica_2_other_film_3),
    .other_4(calcolatore_classifica_2_other_4), .other_film_4(calcolatore_classifica_2_other_film_4),
    .other_5(calcolatore_classifica_2_other_5), .other_film_5(calcolatore_classifica_2_other_film_5),
    .other_6(calcolatore_classifica_2_other_6), .other_film_6(calcolatore_classifica_2_other_film_6),
    .other_7(calcolatore_classifica_2_other_7), .other_film_7(calcolatore_classifica_2_other_film_7),
    .other_8(calcolatore_classifica_2_other_8), .other_film_8(calcolatore_classifica_2_other_film_8),
    .other_9(calcolatore_classifica_2_other_9), .other_film_9(calcolatore_classifica_2_other_film_9),
    .first(calcolatore_classifica_2_first), .first_film(second_film));
  filtro_pre_classifica filtro_pre_classifica_3 (
    .film_da_scartare(second_film), ._0(calcolatore_classifica_2_other),
    .film_0(calcolatore_classifica_2_other_film), ._1(calcolatore_classifica_2_other_2),
    .film_1(calcolatore_classifica_2_other_film_2), ._2(calcolatore_classifica_2_other_3),
    .film_2(calcolatore_classifica_2_other_film_3), ._3(calcolatore_classifica_2_other_4),
    .film_3(calcolatore_classifica_2_other_film_4), ._4(calcolatore_classifica_2_other_5),
    .film_4(calcolatore_classifica_2_other_film_5), ._5(calcolatore_classifica_2_other_6),
    .film_5(calcolatore_classifica_2_other_film_6), ._6(calcolatore_classifica_2_other_7),
    .film_6(calcolatore_classifica_2_other_film_7), ._7(calcolatore_classifica_2_other_8),
    .film_7(calcolatore_classifica_2_other_film_8), ._8(calcolatore_classifica_2_other_9),
    .film_8(calcolatore_classifica_2_other_film_9), ._9(calcolatore_classifica_2_first),
    .film_9(second_film), ._0_2(filtro_pre_classifica_3__0_2), .film_0_2(filtro_pre_classifica_3_film_0_2),
    .out_24(filtro_pre_classifica_3_out_24), .film(filtro_pre_classifica_3_film),
    .out_26(filtro_pre_classifica_3_out_26), .film_10(filtro_pre_classifica_3_film_10),
    .out_28(filtro_pre_classifica_3_out_28), .film_11(filtro_pre_classifica_3_film_11),
    .out_30(filtro_pre_classifica_3_out_30), .film_12(filtro_pre_classifica_3_film_12),
    .out_32(filtro_pre_classifica_3_out_32), .film_13(filtro_pre_classifica_3_film_13),
    .out_34(filtro_pre_classifica_3_out_34), .film_14(filtro_pre_classifica_3_film_14),
    .out_36(filtro_pre_classifica_3_out_36), .film_15(filtro_pre_classifica_3_film_15),
    .out_38(filtro_pre_classifica_3_out_38), .film_16(filtro_pre_classifica_3_film_16),
    .out_40(filtro_pre_classifica_3_out_40), .film_17(filtro_pre_classifica_3_film_17));
  calcolatore_classifica calcolatore_classifica_3 (
    ._0(filtro_pre_classifica_3__0_2), .film_0(filtro_pre_classifica_3_film_0_2),
    ._1(filtro_pre_classifica_3_out_24), .film_1(filtro_pre_classifica_3_film),
    ._2(filtro_pre_classifica_3_out_26), .film_2(filtro_pre_classifica_3_film_10),
    ._3(filtro_pre_classifica_3_out_28), .film_3(filtro_pre_classifica_3_film_11),
    ._4(filtro_pre_classifica_3_out_30), .film_4(filtro_pre_classifica_3_film_12),
    ._5(filtro_pre_classifica_3_out_32), .film_5(filtro_pre_classifica_3_film_13),
    ._6(filtro_pre_classifica_3_out_34), .film_6(filtro_pre_classifica_3_film_14),
    ._7(filtro_pre_classifica_3_out_36), .film_7(filtro_pre_classifica_3_film_15),
    ._8(filtro_pre_classifica_3_out_38), .film_8(filtro_pre_classifica_3_film_16),
    ._9(filtro_pre_classifica_3_out_40), .film_9(filtro_pre_classifica_3_film_17), .first_film(third_film));  // open: other, other_film, other_2, other_film_2, other_3, other_film_3, other_4, other_film_4, other_5, other_film_5, other_6, other_film_6, other_7, other_film_7, other_8, other_film_8, other_9, other_film_9, first

  // Notes on the sheet:
  //   filtro persone a cui è piacuto il film selezionato
endmodule

// ROM
module ROM_opinioni (
  input  [3:0] persona,
  input  [3:0] film,
  output piace
);

  ROM #(.dataWidth(1)) rom_1 (.addr({persona, film}), .data(piace));  // open: sel

  // Notes on the sheet:
  //   gusti persone
  //   contents of rom_1 (hex, n*v repeats v):
  //   0 1 1 0 1 1 0 0 1 1 6*0 1 0 1 0 0 0 1 0 1 1 6*0 1 0 1 0 1 0 1 0 1 8*0 1 0 1 0 0 0 1 1 7*0 1 0 0 1 0
  //   1 1 0 0 1 6*0 1 0 0 1 5*0 1 6*0 1 0 0 1 0 0 0 1 8*0 1 0 0 1 14*0 1 1 0 0 1 1 8*0 1 0 0 1 0 1 0 0 0 1
endmodule

// %
module calcolatore_percentuali (
  input  [3:0] yes,
  input  [3:0] tot,
  output [6:0] out_3
);

  wire [9:0] multiplier_1_out;
  wire [9:7] divider_1_out;

  Multiplier #(.width(10)) multiplier_1 (.a({{6{1'b0}}, yes}), .b(10'h64), .out(multiplier_1_out));  // open: cin, cout
  Divider #(.width(10)) divider_1 (
    .a(multiplier_1_out), .b({{6{1'b0}}, tot}), .out({divider_1_out, out_3}));  // open: upper, rem
  // also tied to GND on the sheet: {divider_1_out[7], divider_1_out[8], divider_1_out[9]}
endmodule

module comparatore_percentuali (
  input  [6:0] percentuale_1,
  input  [6:0] percentuale_2,
  input  [3:0] film_1,
  input  [3:0] film_2,
  output [6:0] percentuale_minore,
  output [6:0] percentuale_maggiore,
  output [3:0] film_minore,
  output [3:0] film_maggiore
);

  wire comparator_1_gt, not_1_out;

  Comparator #(.width(7), .mode("unsigned")) comparator_1 (
    .a(percentuale_1), .b(percentuale_2), .gt(comparator_1_gt));  // open: eq, lt
  Multiplexer #(.width(7), .enable("false")) multiplexer_1 (
    .in0(percentuale_1), .in1(percentuale_2), .out(percentuale_minore), .sel(comparator_1_gt));
  Multiplexer #(.width(7), .enable("false")) multiplexer_2 (
    .in0(percentuale_1), .in1(percentuale_2), .out(percentuale_maggiore), .sel(not_1_out));
  not not_1 (not_1_out, comparator_1_gt);
  Multiplexer #(.width(4), .enable("false")) multiplexer_3 (
    .in0(film_1), .in1(film_2), .out(film_minore), .sel(comparator_1_gt));
  Multiplexer #(.width(4), .enable("false")) multiplexer_4 (
    .in0(film_1), .in1(film_2), .out(film_maggiore), .sel(not_1_out));
endmodule

// filtro
module filtro_pre_classifica (
  input  [3:0] film_da_scartare,
  input  [6:0] _0,
  input  [3:0] film_0,
  input  [6:0] _1,
  input  [3:0] film_1,
  input  [6:0] _2,
  input  [3:0] film_2,
  input  [6:0] _3,
  input  [3:0] film_3,
  input  [6:0] _4,
  input  [3:0] film_4,
  input  [6:0] _5,
  input  [3:0] film_5,
  input  [6:0] _6,
  input  [3:0] film_6,
  input  [6:0] _7,
  input  [3:0] film_7,
  input  [6:0] _8,
  input  [3:0] film_8,
  input  [6:0] _9,
  input  [3:0] film_9,
  output [6:0] _0_2,
  output [3:0] film_0_2,
  output [6:0] out_24,
  output [3:0] film,
  output [6:0] out_26,
  output [3:0] film_10,
  output [6:0] out_28,
  output [3:0] film_11,
  output [6:0] out_30,
  output [3:0] film_12,
  output [6:0] out_32,
  output [3:0] film_13,
  output [6:0] out_34,
  output [3:0] film_14,
  output [6:0] out_36,
  output [3:0] film_15,
  output [6:0] out_38,
  output [3:0] film_16,
  output [6:0] out_40,
  output [3:0] film_17
);

  wire comparator_1_eq, comparator_2_eq, comparator_3_eq, comparator_4_eq, comparator_5_eq, comparator_6_eq,
       comparator_7_eq, comparator_8_eq, comparator_9_eq, comparator_10_eq;

  Multiplexer #(.width(7), .enable("false")) multiplexer_1 (
    .in0(_0), .in1({7{1'b0}}), .out(_0_2), .sel(comparator_1_eq));
  Comparator #(.width(4), .mode("unsigned")) comparator_1 (
    .a(film_0), .b(film_da_scartare), .eq(comparator_1_eq));  // open: gt, lt
  Multiplexer #(.width(7), .enable("false")) multiplexer_2 (
    .in0(_1), .in1({7{1'b0}}), .out(out_24), .sel(comparator_2_eq));
  Comparator #(.width(4), .mode("unsigned")) comparator_2 (
    .a(film_1), .b(film_da_scartare), .eq(comparator_2_eq));  // open: gt, lt
  Multiplexer #(.width(7), .enable("false")) multiplexer_3 (
    .in0(_2), .in1({7{1'b0}}), .out(out_26), .sel(comparator_3_eq));
  Comparator #(.width(4), .mode("unsigned")) comparator_3 (
    .a(film_2), .b(film_da_scartare), .eq(comparator_3_eq));  // open: gt, lt
  Multiplexer #(.width(7), .enable("false")) multiplexer_4 (
    .in0(_3), .in1({7{1'b0}}), .out(out_28), .sel(comparator_4_eq));
  Comparator #(.width(4), .mode("unsigned")) comparator_4 (
    .a(film_3), .b(film_da_scartare), .eq(comparator_4_eq));  // open: gt, lt
  Multiplexer #(.width(7), .enable("false")) multiplexer_5 (
    .in0(_4), .in1({7{1'b0}}), .out(out_30), .sel(comparator_5_eq));
  Comparator #(.width(4), .mode("unsigned")) comparator_5 (
    .a(film_4), .b(film_da_scartare), .eq(comparator_5_eq));  // open: gt, lt
  Multiplexer #(.width(7), .enable("false")) multiplexer_6 (
    .in0(_5), .in1({7{1'b0}}), .out(out_32), .sel(comparator_6_eq));
  Comparator #(.width(4), .mode("unsigned")) comparator_6 (
    .a(film_5), .b(film_da_scartare), .eq(comparator_6_eq));  // open: gt, lt
  Multiplexer #(.width(7), .enable("false")) multiplexer_7 (
    .in0(_6), .in1({7{1'b0}}), .out(out_34), .sel(comparator_7_eq));
  Comparator #(.width(4), .mode("unsigned")) comparator_7 (
    .a(film_6), .b(film_da_scartare), .eq(comparator_7_eq));  // open: gt, lt
  Multiplexer #(.width(7), .enable("false")) multiplexer_8 (
    .in0(_7), .in1({7{1'b0}}), .out(out_36), .sel(comparator_8_eq));
  Comparator #(.width(4), .mode("unsigned")) comparator_8 (
    .a(film_7), .b(film_da_scartare), .eq(comparator_8_eq));  // open: gt, lt
  Multiplexer #(.width(7), .enable("false")) multiplexer_9 (
    .in0(_8), .in1({7{1'b0}}), .out(out_38), .sel(comparator_9_eq));
  Comparator #(.width(4), .mode("unsigned")) comparator_9 (
    .a(film_8), .b(film_da_scartare), .eq(comparator_9_eq));  // open: gt, lt
  Multiplexer #(.width(7), .enable("false")) multiplexer_10 (
    .in0(_9), .in1({7{1'b0}}), .out(out_40), .sel(comparator_10_eq));
  Comparator #(.width(4), .mode("unsigned")) comparator_10 (
    .a(film_9), .b(film_da_scartare), .eq(comparator_10_eq));  // open: gt, lt

  assign film = film_1;
  assign film_0_2 = film_0;
  assign film_10 = film_2;
  assign film_11 = film_3;
  assign film_12 = film_4;
  assign film_13 = film_5;
  assign film_14 = film_6;
  assign film_15 = film_7;
  assign film_16 = film_8;
  assign film_17 = film_9;
endmodule

// classifica
module calcolatore_classifica (
  input  [6:0] _0,
  input  [3:0] film_0,
  input  [6:0] _1,
  input  [3:0] film_1,
  input  [6:0] _2,
  input  [3:0] film_2,
  input  [6:0] _3,
  input  [3:0] film_3,
  input  [6:0] _4,
  input  [3:0] film_4,
  input  [6:0] _5,
  input  [3:0] film_5,
  input  [6:0] _6,
  input  [3:0] film_6,
  input  [6:0] _7,
  input  [3:0] film_7,
  input  [6:0] _8,
  input  [3:0] film_8,
  input  [6:0] _9,
  input  [3:0] film_9,
  output [6:0] other,
  output [3:0] other_film,
  output [6:0] other_2,
  output [3:0] other_film_2,
  output [6:0] other_3,
  output [3:0] other_film_3,
  output [6:0] other_4,
  output [3:0] other_film_4,
  output [6:0] other_5,
  output [3:0] other_film_5,
  output [6:0] other_6,
  output [3:0] other_film_6,
  output [6:0] other_7,
  output [3:0] other_film_7,
  output [6:0] other_8,
  output [3:0] other_film_8,
  output [6:0] other_9,
  output [3:0] other_film_9,
  output [6:0] first,
  output [3:0] first_film
);

  wire [3:0] comparatore_percentuali_1_film_maggiore, comparatore_percentuali_2_film_maggiore,
       comparatore_percentuali_3_film_maggiore, comparatore_percentuali_4_film_maggiore,
       comparatore_percentuali_5_film_maggiore, comparatore_percentuali_6_film_maggiore,
       comparatore_percentuali_7_film_maggiore, comparatore_percentuali_8_film_maggiore;
  wire [6:0] comparatore_percentuali_1_percentuale_maggiore, comparatore_percentuali_2_percentuale_maggiore,
       comparatore_percentuali_3_percentuale_maggiore, comparatore_percentuali_4_percentuale_maggiore,
       comparatore_percentuali_5_percentuale_maggiore, comparatore_percentuali_6_percentuale_maggiore,
       comparatore_percentuali_7_percentuale_maggiore, comparatore_percentuali_8_percentuale_maggiore;

  comparatore_percentuali comparatore_percentuali_1 (
    .percentuale_1(_0), .percentuale_2(_1), .film_1(film_0), .film_2(film_1), .percentuale_minore(other),
    .percentuale_maggiore(comparatore_percentuali_1_percentuale_maggiore), .film_minore(other_film),
    .film_maggiore(comparatore_percentuali_1_film_maggiore));
  comparatore_percentuali comparatore_percentuali_2 (
    .percentuale_1(comparatore_percentuali_1_percentuale_maggiore), .percentuale_2(_2),
    .film_1(comparatore_percentuali_1_film_maggiore), .film_2(film_2), .percentuale_minore(other_2),
    .percentuale_maggiore(comparatore_percentuali_2_percentuale_maggiore), .film_minore(other_film_2),
    .film_maggiore(comparatore_percentuali_2_film_maggiore));
  comparatore_percentuali comparatore_percentuali_3 (
    .percentuale_1(comparatore_percentuali_2_percentuale_maggiore), .percentuale_2(_3),
    .film_1(comparatore_percentuali_2_film_maggiore), .film_2(film_3), .percentuale_minore(other_3),
    .percentuale_maggiore(comparatore_percentuali_3_percentuale_maggiore), .film_minore(other_film_3),
    .film_maggiore(comparatore_percentuali_3_film_maggiore));
  comparatore_percentuali comparatore_percentuali_4 (
    .percentuale_1(comparatore_percentuali_3_percentuale_maggiore), .percentuale_2(_4),
    .film_1(comparatore_percentuali_3_film_maggiore), .film_2(film_4), .percentuale_minore(other_4),
    .percentuale_maggiore(comparatore_percentuali_4_percentuale_maggiore), .film_minore(other_film_4),
    .film_maggiore(comparatore_percentuali_4_film_maggiore));
  comparatore_percentuali comparatore_percentuali_5 (
    .percentuale_1(comparatore_percentuali_4_percentuale_maggiore), .percentuale_2(_5),
    .film_1(comparatore_percentuali_4_film_maggiore), .film_2(film_5), .percentuale_minore(other_5),
    .percentuale_maggiore(comparatore_percentuali_5_percentuale_maggiore), .film_minore(other_film_5),
    .film_maggiore(comparatore_percentuali_5_film_maggiore));
  comparatore_percentuali comparatore_percentuali_6 (
    .percentuale_1(comparatore_percentuali_5_percentuale_maggiore), .percentuale_2(_6),
    .film_1(comparatore_percentuali_5_film_maggiore), .film_2(film_6), .percentuale_minore(other_6),
    .percentuale_maggiore(comparatore_percentuali_6_percentuale_maggiore), .film_minore(other_film_6),
    .film_maggiore(comparatore_percentuali_6_film_maggiore));
  comparatore_percentuali comparatore_percentuali_7 (
    .percentuale_1(comparatore_percentuali_6_percentuale_maggiore), .percentuale_2(_7),
    .film_1(comparatore_percentuali_6_film_maggiore), .film_2(film_7), .percentuale_minore(other_7),
    .percentuale_maggiore(comparatore_percentuali_7_percentuale_maggiore), .film_minore(other_film_7),
    .film_maggiore(comparatore_percentuali_7_film_maggiore));
  comparatore_percentuali comparatore_percentuali_8 (
    .percentuale_1(comparatore_percentuali_7_percentuale_maggiore), .percentuale_2(_8),
    .film_1(comparatore_percentuali_7_film_maggiore), .film_2(film_8), .percentuale_minore(other_8),
    .percentuale_maggiore(comparatore_percentuali_8_percentuale_maggiore), .film_minore(other_film_8),
    .film_maggiore(comparatore_percentuali_8_film_maggiore));
  comparatore_percentuali comparatore_percentuali_9 (
    .percentuale_1(comparatore_percentuali_8_percentuale_maggiore), .percentuale_2(_9),
    .film_1(comparatore_percentuali_8_film_maggiore), .film_2(film_9), .percentuale_minore(other_9),
    .percentuale_maggiore(first), .film_minore(other_film_9), .film_maggiore(first_film));
endmodule

module TTY_scelti_per_te (
  input  risultati,
  input  clock,
  input  [3:0] first_f,
  input  [3:0] second_f,
  input  [3:0] third_f,
  input  cancella,
  output [6:0] ascii
);

  wire and_1_out, and_2_out, and_3_out, and_4_out, counter_1_carry, or_1_out;
  wire [1:0] counter_1_q;
  wire [3:0] multiplexer_1_out;
  wire [4:0] counter_2_q;

  and and_1 (and_1_out, risultati, ~clock);  // AND_Gate
  Multiplexer #(.select(2), .width(4), .enable("false")) multiplexer_1 (
    .in0(first_f), .in1(second_f), .in2(third_f), .in3(4'b1111), .out(multiplexer_1_out), .sel(counter_1_q));
  Counter #(.width(2), .max('h3), .ongoal("stay"), .trigger("falling")) counter_1 (
    .Q(counter_1_q), .carry(counter_1_carry), .clk(and_2_out), .clr(cancella));  // open: load, D, count
  and and_2 (and_2_out, risultati, clock, and_4_out);
  Counter #(.width(5), .max('h1c), .ongoal("stay"), .trigger("falling")) counter_2 (
    .Q(counter_2_q), .clk(and_1_out), .clr(or_1_out));  // open: load, D, count, carry
  or or_1 (or_1_out, and_3_out, cancella);
  and and_3 (and_3_out, ~counter_1_carry, and_4_out);  // AND_Gate
  ROM_ascii rom_ascii_1 (.char(counter_2_q), .titolo(multiplexer_1_out), .ascii(ascii));
  and and_4 (and_4_out, ~ascii[6], ~ascii[5], ~ascii[4], ~ascii[3], ~ascii[2], ~ascii[1], ~ascii[0]);  // AND_Gate

  // Notes on the sheet:
  //   fine stringa
endmodule
